# Fritzing sketch microcontroller HAM radio 20m QRP (saved by Fritzing 0.9.3b)
breadboards: 3

parts:
  M1 = ESP32-S3-DevKitC-1-N8R8-v1 [part_number=ESP32-S3-DevKitC-1-N8R8-v1]
  Bauteil1 = Adafruit Si5351A Clock Generator [part_number="Adafruit #2045"]
  SW1 = ENCODER_RGB_CA [package=encoder_led_3]
  U1 = SD_CARD_SOCKET [package=sdcard_4uconn]  # not connected
  TRS1 = Audio Jack (TRS) 3.5mm [package="4Ucon 08780 [THT]"]
  LCD1 = TFT 3.5 inch 480x320 w touch and SD

nets:
  N1: M1.pin_1, M1.pin_2, Bauteil1.VIN, SW1.B, LCD1.Pin_1
  N2: M1.pin_12, Bauteil1.SDA
  N3: M1.pin_14, LCD1.Pin_8
  N4: M1.pin_15, Bauteil1.SCL
  N5: M1.pin_16, LCD1.Pin_7
  N6: M1.pin_17, LCD1.Pin_6
  N7: M1.pin_18, LCD1.Pin_5
  N8: M1.pin_19, LCD1.Pin_4
  N9: M1.pin_20, LCD1.Pin_3
  N10: M1.pin_22, M1.pin_23, M1.pin_24, M1.pin_44, Bauteil1.GND, SW1.C, LCD1.Pin_2
  N11: M1.pin_34, TRS1.Tip
  N12: M1.pin_36, SW1.A
  N13: M1.pin_37, SW1.+
  N14: M1.pin_38, SW1.-B

custom parts:
  ESP32-S3-DevKitC-1-N8R8-v1: ESP32-S3-DevKitC-1-N8R8-v1 This module is 44pins long (2x22) and 11 pins width.
  Adafruit Si5351A Clock Generator: Never hunt around for another crystal again, with the Si5351A clock generator breakout from Adafruit! This chip has a precision 25MHz crystal reference and internal PLL and dividers so it can generate just about any frequency, from <8KHz up to 150+ MHz. The Si5351A clock generator is an I2C controller clock generator. It uses the onboard precision clock to drive multiple PLL's and clock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
  TFT 3.5 inch 480x320 w touch and SD: This is a generic 1.8 tft spi lcd display available on ebay and others. The 1.8"3.5 inch 480X320 SPI TFT Module 320x480 LCD Display - Touch.
